// Logisim project LogisimTPGroupe7.circ as structural Verilog: 1 circuit, main circuit main
module main (
  input  A,
  input  B,
  input  C,
  input  D,
  input  in_5,
  output out_6,
  output out_7
);

  wire and_1_out, and_3_out, and_4_out, and_5_out, and_6_out, and_7_out, not_1_out, not_2_out, not_3_out,
       not_4_out, not_5_out, or_1_out, or_2_out, or_3_out;

  not not_1 (not_1_out, in_5);
  not not_2 (not_2_out, B);
  not not_3 (not_3_out, D);
  and and_1 (and_1_out, A, not_2_out);
  and and_2 (out_7, not_1_out, in_5);
  and and_3 (and_3_out, and_1_out, C);
  and and_4 (and_4_out, A, not_3_out);
  or or_1 (or_1_out, and_3_out, and_4_out);
  not not_4 (not_4_out, C);
  or or_2 (or_2_out, B, not_4_out);
  and and_5 (and_5_out, or_1_out, or_2_out);
  not not_5 (not_5_out, A);
  or or_3 (or_3_out, not_5_out, D);
  and and_6 (and_6_out, and_5_out, or_3_out);
  and and_7 (and_7_out, not_2_out, C);
  and and_8 (out_6, and_6_out, and_7_out);
endmodule
